# Fritzing sketch схема (saved by Fritzing 0.9.3b)
breadboards: 2

parts:
  Часть1 = Arduino Nano (Rev3.0)
  Disp1 = LBT2088AH [part_number=LBT2088AH]
  S1 = Pushbutton [package="[THT]"]
  S2 = Pushbutton [package="[THT]"]
  S3 = Pushbutton [package="[THT]"]
  S4 = Pushbutton [package="[THT]"]

nets:
  N1: Часть1.D2, Disp1.pin_7
  N2: Часть1.D3, S1.Pin_1, S1.Pin_2
  N3: Часть1.D4, S4.Pin_1, S4.Pin_2
  N4: Часть1.D5, S3.Pin_1, S3.Pin_2
  N5: Часть1.D6, S2.Pin_1, S2.Pin_2
  N6: Disp1.pin_6, S1.Pin_3, S1.Pin_4, S2.Pin_3, S2.Pin_4, S3.Pin_3, S3.Pin_4, S4.Pin_3, S4.Pin_4
